# Fritzing sketch client_esp_8266 (saved by Fritzing 0.9.5d)
breadboards: 1

parts:
  S4 = Pushbutton [package="[THT]"]
  OLED_I2C1 = OLED 128x64 I2C Monochrome Display
  R1 = Resistor [tolerance=±5% resistance=220 package=THT]
  LED1 = smd LED [color="Red (633nm)" package="1206 [SMD]"]
  R2 = Resistor [tolerance=±5% resistance=220 package=THT]
  U4 = NodeMCU V1.0
  J1 = Piezo Speaker

nets:
  N1: S4.Pin_1, S4.Pin_2, R1.Pin_0, U4.D8
  VDD: S4.Pin_3, S4.Pin_4, OLED_I2C1.VDD, R2.Pin_1, U4.3V3
  N2: OLED_I2C1.SDA, U4.D2
  N3: OLED_I2C1.SCK, U4.D1
  GND: OLED_I2C1.GND, R1.Pin_1, U4.GND, J1.pin1
  N4: LED1.cathode, R2.Pin_0
  N5: LED1.anode, U4.D4
  N6: U4.D6, J1.pin2

custom parts:
  NodeMCU V1.0: ESP8266 based NodeMCU
